# Fritzing sketch SelectablePD (saved by Fritzing 1.0.4)

parts:
  Part1 = Arduino Uno (Rev3)
  Part2 = OLED Monochrome 128x32 I2C [part_number=931]
  Adafruit_HUSB238_USB-C_PD_Breakout1 = Adafruit HUSB238 USB-C PD Breakout [part_number=#5807]
  S1 = Square Pushbutton
  S2 = Square Pushbutton
  S3 = Square Pushbutton
  S4 = Square Pushbutton
  LED1 = smd LED [color="Red (633nm)" package="0805 [SMD]"]
  LED2 = smd LED [color="Red (633nm)" package="0805 [SMD]"]
  LED3 = smd LED [color="Red (633nm)" package="0805 [SMD]"]
  LED4 = smd LED [color="Red (633nm)" package="0805 [SMD]"]
  R1 = Resistor [tolerance=±5% power=0.25W resistance=330 package=THT]
  R2 = Resistor [tolerance=±5% power=0.25W resistance=10k package=THT]
  R3 = Resistor [tolerance=±5% power=0.25W resistance=10k package=THT]
  R4 = Resistor [tolerance=±5% power=0.25W resistance=10k package=THT]
  R5 = Resistor [tolerance=±5% power=0.25W resistance=10k package=THT]

nets:
  N1: Part1.A4/SDA, Part2.SDA, Adafruit_HUSB238_USB-C_PD_Breakout1.SDA
  N2: Part1.A5/SCL, Part2.SCL, Adafruit_HUSB238_USB-C_PD_Breakout1.SCL
  N3: Part1.D9_PWM, LED4.anode
  N4: Part1.D10_PWM/SS, LED3.anode
  N5: Part1.D11_PWM/MOSI, LED2.anode
  N6: Part1.D12/MISO, LED1.anode
  GND: Part1.GND, Part2.GND, Adafruit_HUSB238_USB-C_PD_Breakout1.GND, R1.Pin_0, R2.Pin_0, R3.Pin_0, R4.Pin_0, R5.Pin_0
  N7: Part1.D2, S4.leg0, R5.Pin_1
  N8: Part1.D3_PWM, S3.leg0, R4.Pin_1
  N9: Part1.D4, S2.leg0, R3.Pin_1
  N10: Part1.D5_PWM, S1.leg0, R2.Pin_1
  5V: Part1.5V, Part2.VIN, Adafruit_HUSB238_USB-C_PD_Breakout1.VOUT, S1.leg1, S2.leg1, S3.leg1, S4.leg1
  N11: LED1.cathode, LED2.cathode, LED3.cathode, LED4.cathode, R1.Pin_1

custom parts:
  OLED Monochrome 128x32 I2C: These displays are small, only about 1" diagonal, but very readable due to the high contrast of an OLED display. This display is made of 128x32 individual white OLED pixels, each one is turned on or off by the controller chip. Because the display makes its own light, no backlight is required. This reduces the power required to run the OLED and is why the display has such high contrast; we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
  Adafruit HUSB238 USB-C PD Breakout: The HUSB238 USB PD sink chip is neat in that you can either use jumpers (really, resistor selection) to set the desired PD voltage and current or you can use I2C for dynamic querying and setting. We've build a nice Adafruit USB Type C Power Delivery Dummy Breakout board around the HUSB238 to make it very easy to configure and integrate without having to solder any tiny resistors. It's perfect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
